// Logisim project gdh12_project3.circ as structural Verilog: 11 circuits, main circuit main
module main (
  input  Reset,
  output out_2,
  output [1:0] RS,
  output [1:0] RT,
  output [1:0] RD,
  output [1:0] Write_Reg,
  output [7:0] Imm,
  output [7:0] out_8
);

  wire alu_1_zero, and_1_out, branch_control_1_tobranch, clock_1_out, control2_1_branch, control2_1_eq,
       control2_1_halt, control2_1_jump, control2_1_updatedisplay, control_1_ainvert, control_1_alusrc,
       control_1_bnegate, control_1_memtoreg, control_1_memwrite, control_1_regdst, instruction_memory_1_op0,
       instruction_memory_1_op1, instruction_memory_1_op2, instruction_memory_1_op3, not_1_out;
  wire [1:0] alu_control_1_aluop0;
  wire [7:0] adder_1_out, adder_2_out, alu_1_alu_result, data_memory_1_display_0, data_memory_1_display_1,
       data_memory_1_display_2, data_memory_1_display_3, data_memory_1_display_4, data_memory_1_display_5,
       data_memory_1_display_6, data_memory_1_display_7, data_memory_1_read_data, multiplexer_2_out,
       multiplexer_3_out, multiplexer_4_out, multiplexer_5_out, register_1_q, register_2_read_data_1;

  Register_part register_1 (.D(multiplexer_4_out), .Q(register_1_q), .clk(and_1_out), .clr(Reset));  // open: en
  Instruction_Memory instruction_memory_1 (
    .Op3(instruction_memory_1_op3), .Op2(instruction_memory_1_op2), .Op1(instruction_memory_1_op1),
    .Op0(instruction_memory_1_op0), .RS(RS), .RT(RT), .RD(RD), .Immediate(Imm), .Address(register_1_q),
    .Clock(and_1_out));
  and and_1 (and_1_out, clock_1_out, not_1_out);
  Clock clock_1 (.out(clock_1_out));
  not not_1 (not_1_out, control2_1_halt);
  Adder adder_1 (.a(register_1_q), .b(8'h1), .out(adder_1_out));  // open: cin, cout
  Control control_1 (
    .Op3(instruction_memory_1_op3), .Op2(instruction_memory_1_op2), .Op1(instruction_memory_1_op1),
    .Op0(instruction_memory_1_op0), .MemtoReg(control_1_memtoreg), .RegWrite(out_2),
    .ALUsrc(control_1_alusrc), .RegDst(control_1_regdst), .Ainvert(control_1_ainvert),
    .Bnegate(control_1_bnegate), .MemWrite(control_1_memwrite));  // open: ALUop2, ALUop1, Bnegate_2
  Control2 control2_1 (
    .Op3(instruction_memory_1_op3), .Op2(instruction_memory_1_op2), .Op1(instruction_memory_1_op1),
    .Op0(instruction_memory_1_op0), .Branch(control2_1_branch), .EQ(control2_1_eq), .Jump(control2_1_jump),
    .UpdateDIsplay(control2_1_updatedisplay), .Halt(control2_1_halt));
  ALU_Control alu_control_1 (
    .op3(instruction_memory_1_op3), .op2(instruction_memory_1_op2), .op1(instruction_memory_1_op1),
    .op0(instruction_memory_1_op0), .ALUop1(alu_control_1_aluop0[1]), .ALUop0(alu_control_1_aluop0[0]));
  Multiplexer #(.width(2)) multiplexer_1 (.in0(RD), .in1(RT), .out(Write_Reg), .sel(control_1_regdst));
  Register register_2 (
    .ReadReg1(RS), .ReadReg2(RT), .WriteReg(Write_Reg), .Write_Data(multiplexer_5_out), .RegWrite(out_2),
    .Clock(and_1_out), .Read_Data_1(register_2_read_data_1), .Read_Data_2(out_8));
  Multiplexer #(.width(8)) multiplexer_2 (.in0(out_8), .in1(Imm), .out(multiplexer_2_out), .sel(control_1_alusrc));
  ALU alu_1 (
    .Input_1(register_2_read_data_1), .Input_2(multiplexer_2_out), .ALU_result(alu_1_alu_result),
    .ZERO(alu_1_zero), .ALUop(alu_control_1_aluop0), .Ainvert(control_1_ainvert), .Binvert(control_1_bnegate));
  Data_Memory data_memory_1 (
    .Address(alu_1_alu_result), .Write_Data(out_8), .Clock(and_1_out), .Read_Data(data_memory_1_read_data),
    .Memwrite(control_1_memwrite), .Update_Display(control2_1_updatedisplay),
    .Display_0(data_memory_1_display_0), .Display_1(data_memory_1_display_1),
    .Display_2(data_memory_1_display_2), .Display_3(data_memory_1_display_3),
    .Display_4(data_memory_1_display_4), .Display_7(data_memory_1_display_7),
    .Display_5(data_memory_1_display_5), .Display_6(data_memory_1_display_6));  // open: MemRead
  Adder adder_2 (.a(adder_1_out), .b(Imm), .out(adder_2_out));  // open: cin, cout
  Branch_Control branch_control_1 (
    .Branch(control2_1_branch), .EQ(control2_1_eq), .Zero(alu_1_zero), .ToBranch(branch_control_1_tobranch));
  Multiplexer #(.width(8)) multiplexer_3 (
    .in0(adder_1_out), .in1(adder_2_out), .out(multiplexer_3_out), .sel(branch_control_1_tobranch));
  DotMatrix #(.matrixcols(8), .matrixrows(8), .dotshape("circle")) dotmatrix_1 (
    .col0(data_memory_1_display_0), .col1(data_memory_1_display_1), .col2(data_memory_1_display_2),
    .col3(data_memory_1_display_3), .col4(data_memory_1_display_4), .col5(data_memory_1_display_5),
    .col6(data_memory_1_display_6), .col7(data_memory_1_display_7));
  Multiplexer #(.width(8)) multiplexer_4 (
    .in0(multiplexer_3_out), .in1(Imm), .out(multiplexer_4_out), .sel(control2_1_jump));
  Multiplexer #(.width(8)) multiplexer_5 (
    .in0(alu_1_alu_result), .in1(data_memory_1_read_data), .out(multiplexer_5_out), .sel(control_1_memtoreg));
endmodule

module Instruction_Memory (
  input  [7:0] Address,
  input  Clock,
  output Op3,
  output Op2,
  output Op1,
  output Op0,
  output [1:0] RS,
  output [1:0] RT,
  output [1:0] RD,
  output [7:0] Immediate
);

  ROM #(.dataWidth(16)) rom_1 (.addr(Address), .data({Op3, Op2, Op1, Op0, RS, RT, Immediate}), .sel(1'b1));

  assign RD = Immediate[7:6];

  // Notes on the sheet:
  //   contents of rom_1 (hex, n*v repeats v):
  //   4508 8110 417f 4208 8d80 4aff 4f01 9000 32fb 9000 6040 4501 4208 8d80 4aff 4f01 9000 32fb 540 4501
  //   c210 8111 c112 5904 4501 8112 c111 b00c f000
endmodule

module Control (
  input  Op3,
  input  Op2,
  input  Op1,
  input  Op0,
  output ALUop2,
  output ALUop1,
  output MemtoReg,
  output RegWrite,
  output ALUsrc,
  output RegDst,
  output Ainvert,
  output Bnegate,
  output Bnegate_2,
  output MemWrite
);

  wire and_1_out, and_2_out, and_3_out, and_4_out, and_5_out, and_7_out, and_8_out, and_9_out, and_13_out,
       and_14_out, and_15_out, not_1_out, not_2_out, not_3_out, not_4_out, not_5_out, not_6_out, not_7_out,
       not_8_out, not_9_out, not_10_out, not_11_out, not_12_out, not_13_out, not_14_out, not_15_out,
       not_16_out, not_17_out, not_18_out, not_19_out, not_20_out, not_21_out, not_22_out, not_23_out,
       not_24_out, not_25_out, not_26_out, not_27_out, not_28_out, not_29_out, not_30_out, not_31_out,
       not_32_out, undriven, undriven_2, undriven_3, undriven_4;

  not not_1 (not_1_out, Op1);
  not not_2 (not_2_out, Op0);
  not not_3 (not_3_out, Op3);
  and and_1 (and_1_out, not_3_out, not_4_out, not_5_out);
  not not_4 (not_4_out, Op2);
  not not_5 (not_5_out, Op1);
  not not_6 (not_6_out, Op3);
  and and_2 (and_2_out, not_6_out, not_7_out);
  not not_7 (not_7_out, Op0);
  not not_8 (not_8_out, Op1);
  and and_3 (and_3_out, Op2, not_8_out, not_9_out);
  not not_9 (not_9_out, Op0);
  and and_4 (and_4_out, Op2, not_10_out, not_11_out);
  not not_10 (not_10_out, Op1);
  not not_11 (not_11_out, Op0);
  and and_5 (and_5_out, Op3, not_12_out, not_13_out);
  not not_12 (not_12_out, Op1);
  not not_13 (not_13_out, Op0);
  and and_6 (RegDst, Op2, not_14_out, not_15_out);
  not not_14 (not_14_out, Op1);
  not not_15 (not_15_out, Op0);
  not not_16 (not_16_out, Op3);
  not not_17 (not_17_out, Op0);
  not not_18 (not_18_out, Op3);
  not not_19 (not_19_out, Op1);
  and and_7 (and_7_out, not_18_out, not_19_out, Op0);
  not not_20 (not_20_out, Op3);
  and and_8 (and_8_out, not_20_out, not_21_out, Op1);
  not not_21 (not_21_out, Op2);
  not not_22 (not_22_out, Op3);
  and and_9 (and_9_out, not_22_out, Op1, not_23_out);
  not not_23 (not_23_out, Op0);
  not not_24 (not_24_out, Op2);
  not not_25 (not_25_out, Op1);
  not not_26 (not_26_out, Op0);
  and and_10 (MemtoReg, Op3, Op2, not_1_out, not_2_out);
  or or_1 (RegWrite, and_1_out, and_2_out, and_3_out);
  or or_2 (ALUsrc, and_4_out, and_5_out);
  and and_11 (Ainvert, not_16_out, Op2, Op1, not_17_out);
  or or_3 (Bnegate, and_7_out, and_8_out, and_9_out);
  and and_12 (MemWrite, Op3, not_24_out, not_25_out, not_26_out);
  // NOT_Gate extra is placed but not wired
  not not_27 (not_27_out, undriven);
  not not_28 (not_28_out, undriven_2);
  not not_29 (not_29_out, undriven);
  not not_30 (not_30_out, undriven_2);
  not not_31 (not_31_out, undriven);
  not not_32 (not_32_out, undriven_4);
  and and_13 (and_13_out, not_27_out, not_28_out, undriven_3);
  and and_14 (and_14_out, not_29_out, not_30_out, undriven_4);
  and and_15 (and_15_out, not_31_out, undriven_2, not_32_out);
  or or_4 (Bnegate_2, and_13_out, and_14_out, and_15_out);
endmodule

module Register (
  input  RegWrite,
  input  [1:0] ReadReg1,
  input  [1:0] WriteReg,
  input  [1:0] ReadReg2,
  input  [7:0] Write_Data,
  input  Clock,
  output [7:0] Read_Data_1,
  output [7:0] Read_Data_2
);

  wire demultiplexer_1_out1, demultiplexer_1_out2, demultiplexer_1_out3;
  wire [7:0] r1_q, r2_q, r3_q;

  Demultiplexer #(.select(2)) demultiplexer_1 (
    .out1(demultiplexer_1_out1), .out2(demultiplexer_1_out2), .out3(demultiplexer_1_out3), .in(RegWrite),
    .sel(WriteReg));  // open: out0
  Register_part r1 (.D(Write_Data), .en(demultiplexer_1_out1), .Q(r1_q), .clk(Clock));  // open: clr
  Register_part r2 (.D(Write_Data), .en(demultiplexer_1_out2), .Q(r2_q), .clk(Clock));  // open: clr
  Register_part r3 (.D(Write_Data), .en(demultiplexer_1_out3), .Q(r3_q), .clk(Clock));  // open: clr
  Multiplexer #(.select(2), .width(8)) multiplexer_1 (
    .in0({8{1'b0}}), .in1(r1_q), .in2(r2_q), .in3(r3_q), .out(Read_Data_1), .sel(ReadReg1));
  Multiplexer #(.select(2), .width(8)) multiplexer_2 (
    .in0({8{1'b0}}), .in1(r1_q), .in2(r2_q), .in3(r3_q), .out(Read_Data_2), .sel(ReadReg2));
endmodule

module Data_Memory (
  input  Memwrite,
  input  [7:0] Address,
  input  MemRead,
  input  [7:0] Write_Data,
  input  Clock,
  input  Update_Display,
  output [7:0] Read_Data,
  output [7:0] Display_0,
  output [7:0] Display_1,
  output [7:0] Display_2,
  output [7:0] Display_3,
  output [7:0] Display_4,
  output [7:0] Display_5,
  output [7:0] Display_6,
  output [7:0] Display_7
);

  wire and_1_out, not_1_out, not_2_out;
  wire [7:0] controlled_buffer_1_out, undriven;

  not not_1 (not_1_out, Address[7]);
  not not_2 (not_2_out, Memwrite);
  and and_1 (and_1_out, Address[7], Memwrite);
  assign controlled_buffer_1_out = Memwrite ? Write_Data : 8'bz;  // Controlled_Buffer controlled_buffer_1
  RAM #(.addrWidth(7)) ram_1 (
    .addr(Address[6:0]), .data(controlled_buffer_1_out), .sel(not_1_out), .clk(Clock), .ld(not_2_out));  // open: clr
  Multiplexer #(.width(8)) multiplexer_1 (
    .in0(controlled_buffer_1_out), .in1(undriven), .out(Read_Data), .sel(Address[7]));
  IO_register io_register_1 (
    .Write_Data(Write_Data), .IORegister(Address[2:0]), .Memwrite(and_1_out), .Clock(Clock),
    .Display(Update_Display), .Data(undriven), .Display_1(Display_0), .Display_2(Display_1),
    .Display_3(Display_2), .Display_4(Display_3), .Display_5(Display_4), .Display_6(Display_5),
    .Display_7(Display_6), .Display_8(Display_7));
endmodule

module ALU (
  input  [7:0] Input_1,
  input  Ainvert,
  input  [7:0] Input_2,
  input  Binvert,
  input  [1:0] ALUop,
  output ZERO,
  output [7:0] ALU_result
);

  wire or_2_out;
  wire [7:0] adder_1_out, and_1_out, bit_extender_1_out, multiplexer_1_out, multiplexer_2_out, not_1_out,
       not_2_out, or_1_out;

  Multiplexer #(.width(8)) multiplexer_1 (.in0(Input_1), .in1(not_1_out), .out(multiplexer_1_out), .sel(Ainvert));
  assign not_1_out = ~Input_1;  // NOT_Gate not_1, 8 bits wide
  Multiplexer #(.width(8)) multiplexer_2 (.in0(Input_2), .in1(not_2_out), .out(multiplexer_2_out), .sel(Binvert));
  assign not_2_out = ~Input_2;  // NOT_Gate not_2, 8 bits wide
  assign and_1_out = multiplexer_1_out & multiplexer_2_out;  // AND_Gate and_1, 8 bits wide
  assign or_1_out = multiplexer_1_out | multiplexer_2_out;  // OR_Gate or_1, 8 bits wide
  Adder adder_1 (.a(multiplexer_1_out), .b(multiplexer_2_out), .out(adder_1_out), .cin(Binvert));  // open: cout
  Multiplexer #(.select(2), .width(8)) multiplexer_3 (
    .in0(and_1_out), .in1(or_1_out), .in2(adder_1_out), .in3(bit_extender_1_out), .out(ALU_result),
    .sel(ALUop));
  assign bit_extender_1_out = {{7{1'b0}}, adder_1_out[7]};  // Bit_Extender bit_extender_1
  not not_3 (ZERO, or_2_out);
  or or_2 (or_2_out, ALU_result[7], ALU_result[6], ALU_result[5], ALU_result[4], ALU_result[2], ALU_result[1], ALU_result[0], ALU_result[3]);
endmodule

module IO_register (
  input  [7:0] Write_Data,
  input  [7:0] Data,
  input  [2:0] IORegister,
  input  Memwrite,
  input  Clock,
  input  Display,
  output [7:0] Display_1,
  output [7:0] Display_2,
  output [7:0] Display_3,
  output [7:0] Display_4,
  output [7:0] Display_5,
  output [7:0] Display_6,
  output [7:0] Display_7,
  output [7:0] Display_8
);

  wire and_1_out, and_2_out, and_3_out, and_4_out, and_5_out, and_6_out, and_7_out, and_8_out,
       decoder_1_out0, decoder_1_out1, decoder_1_out2, decoder_1_out3, decoder_1_out4, decoder_1_out5,
       decoder_1_out6, decoder_1_out7;
  wire [7:0] register_1_q, register_2_q, register_3_q, register_4_q, register_5_q, register_6_q,
       register_7_q, register_8_q;

  Decoder #(.select(3)) decoder_1 (
    .out0(decoder_1_out0), .out1(decoder_1_out1), .out2(decoder_1_out2), .out3(decoder_1_out3),
    .out4(decoder_1_out4), .out5(decoder_1_out5), .out6(decoder_1_out6), .out7(decoder_1_out7),
    .sel(IORegister));
  and and_1 (and_1_out, decoder_1_out0, Memwrite);
  and and_2 (and_2_out, decoder_1_out1, Memwrite);
  and and_3 (and_3_out, decoder_1_out2, Memwrite);
  and and_4 (and_4_out, decoder_1_out3, Memwrite);
  and and_5 (and_5_out, decoder_1_out4, Memwrite);
  and and_6 (and_6_out, decoder_1_out5, Memwrite);
  and and_7 (and_7_out, decoder_1_out6, Memwrite);
  and and_8 (and_8_out, decoder_1_out7, Memwrite);
  Register_part register_1 (.D(Write_Data), .en(and_1_out), .Q(register_1_q), .clk(Clock));  // open: clr
  Register_part register_2 (.D(Write_Data), .en(and_2_out), .Q(register_2_q), .clk(Clock));  // open: clr
  Register_part register_3 (.D(Write_Data), .en(and_3_out), .Q(register_3_q), .clk(Clock));  // open: clr
  Register_part register_4 (.D(Write_Data), .en(and_4_out), .Q(register_4_q), .clk(Clock));  // open: clr
  Register_part register_5 (.D(Write_Data), .en(and_5_out), .Q(register_5_q), .clk(Clock));  // open: clr
  Register_part register_6 (.D(Write_Data), .en(and_6_out), .Q(register_6_q), .clk(Clock));  // open: clr
  Register_part register_7 (.D(Write_Data), .en(and_7_out), .Q(register_7_q), .clk(Clock));  // open: clr
  Register_part register_8 (.D(Write_Data), .en(and_8_out), .Q(register_8_q), .clk(Clock));  // open: clr
  Multiplexer #(.select(3), .width(8)) multiplexer_1 (
    .in0(register_1_q), .in1(register_2_q), .in2(register_3_q), .in3(register_4_q), .in4(register_5_q),
    .in5(register_6_q), .in6(register_7_q), .in7(register_8_q), .out(Data), .sel(IORegister));
  Register_part register_9 (.D(register_1_q), .en(Display), .Q(Display_1), .clk(Clock));  // open: clr
  Register_part register_10 (.D(register_2_q), .en(Display), .Q(Display_2), .clk(Clock));  // open: clr
  Register_part register_11 (.D(register_3_q), .en(Display), .Q(Display_3), .clk(Clock));  // open: clr
  Register_part register_12 (.D(register_4_q), .en(Display), .Q(Display_4), .clk(Clock));  // open: clr
  Register_part register_13 (.D(register_5_q), .en(Display), .Q(Display_5), .clk(Clock));  // open: clr
  Register_part register_14 (.D(register_6_q), .en(Display), .Q(Display_6), .clk(Clock));  // open: clr
  Register_part register_15 (.D(register_7_q), .en(Display), .Q(Display_7), .clk(Clock));  // open: clr
  Register_part register_16 (.D(register_8_q), .en(Display), .Q(Display_8), .clk(Clock));  // open: clr
endmodule

module Branch_Control (
  input  Branch,
  input  EQ,
  input  Zero,
  output ToBranch
);

  wire and_1_out, and_2_out, not_1_out, not_2_out;

  not not_1 (not_1_out, EQ);
  not not_2 (not_2_out, Zero);
  and and_1 (and_1_out, Branch, not_1_out, not_2_out);
  and and_2 (and_2_out, Branch, EQ, Zero);
  or or_1 (ToBranch, and_1_out, and_2_out);
endmodule

module Control2 (
  input  Op3,
  input  Op2,
  input  Op1,
  input  Op0,
  output Branch,
  output EQ,
  output Jump,
  output UpdateDIsplay,
  output Halt
);

  wire and_2_out, and_3_out, not_1_out, not_2_out, not_3_out, not_4_out, not_5_out, not_6_out, not_7_out,
       not_8_out, not_9_out;

  not not_1 (not_1_out, Op3);
  not not_2 (not_2_out, Op2);
  not not_3 (not_3_out, Op3);
  not not_4 (not_4_out, Op1);
  not not_5 (not_5_out, Op3);
  not not_6 (not_6_out, Op1);
  not not_7 (not_7_out, Op2);
  not not_8 (not_8_out, Op2);
  not not_9 (not_9_out, Op1);
  and and_1 (Halt, Op3, Op2, Op1, Op0);
  and and_2 (and_2_out, not_1_out, not_2_out, Op1, Op0);
  or or_1 (Branch, and_2_out, and_3_out);
  and and_3 (and_3_out, not_3_out, Op2, not_4_out, Op0);
  and and_4 (EQ, not_5_out, Op2, not_6_out, Op0);
  and and_5 (Jump, Op3, not_7_out, Op1, Op0);
  and and_6 (UpdateDIsplay, Op3, not_8_out, not_9_out, Op0);
endmodule

module test (
  input  op3,
  input  op2,
  input  op1,
  input  op0,
  output Bnegate
);

  wire and_1_out, and_2_out, and_3_out, not_1_out, not_2_out, not_3_out, not_4_out, not_5_out, not_6_out;

  not not_1 (not_1_out, op3);
  and and_1 (and_1_out, not_1_out, not_2_out, op0);
  not not_2 (not_2_out, op2);
  not not_3 (not_3_out, op3);
  and and_2 (and_2_out, not_3_out, not_4_out, op1);
  not not_4 (not_4_out, op2);
  not not_5 (not_5_out, op3);
  and and_3 (and_3_out, not_5_out, op2, not_6_out);
  not not_6 (not_6_out, op1);
  or or_1 (Bnegate, and_1_out, and_2_out, and_3_out);
endmodule

module ALU_Control (
  input  op3,
  input  op2,
  input  op1,
  input  op0,
  output ALUop1,
  output ALUop0
);

  wire and_1_out, and_2_out, and_3_out, not_1_out, not_2_out, not_3_out, not_4_out, not_5_out, not_6_out,
       not_7_out, not_8_out;

  not not_1 (not_1_out, op3);
  and and_1 (and_1_out, not_1_out, not_2_out);
  not not_2 (not_2_out, op2);
  not not_3 (not_3_out, op3);
  and and_2 (and_2_out, not_3_out, not_4_out);
  not not_4 (not_4_out, op1);
  not not_5 (not_5_out, op1);
  and and_3 (and_3_out, not_5_out, not_6_out);
  not not_6 (not_6_out, op0);
  not not_7 (not_7_out, op3);
  and and_4 (ALUop0, not_7_out, op1, not_8_out);
  not not_8 (not_8_out, op0);
  or or_1 (ALUop1, and_1_out, and_2_out, and_3_out);
endmodule
